// Logisim project AND Gate (CMOS).circ as structural Verilog: 1 circuit, main circuit main
module main (
);

  wire nand_1_out, nand_2_out;

  nand nand_1 (nand_1_out, 1'b0, 1'b0);
  // Probe on nand_2_out
  nand nand_2 (nand_2_out, nand_1_out, nand_1_out);
endmodule
