// Logisim project AND Gate.circ as structural Verilog: 1 circuit, main circuit main
module main (
);

  wire transistor_1_out, transistor_3_out, transistor_5_out, transistor_7_out;

  Transistor transistor_1 (.in(1'b1), .out(transistor_1_out), .gate(1'b1));
  Transistor #(.\type ("n")) transistor_2 (.in(transistor_3_out), .out(transistor_1_out), .gate(1'b1));
  Transistor #(.\type ("n")) transistor_3 (.in(1'b0), .out(transistor_3_out), .gate(1'b1));
  Transistor transistor_4 (.in(1'b1), .out(transistor_1_out), .gate(1'b1));
  // Probe on transistor_1_out
  Transistor transistor_5 (.in(1'b1), .out(transistor_5_out), .gate(transistor_1_out));
  Transistor #(.\type ("n")) transistor_6 (.in(transistor_7_out), .out(transistor_5_out), .gate(transistor_1_out));
  Transistor #(.\type ("n")) transistor_7 (.in(1'b0), .out(transistor_7_out), .gate(transistor_1_out));
  Transistor transistor_8 (.in(1'b1), .out(transistor_5_out), .gate(transistor_1_out));
  // Probe on transistor_5_out
endmodule
