// Logisim project OR Gate (CMOS).circ as structural Verilog: 1 circuit, main circuit main
module main (
);

  wire nand_1_out, nand_2_out, nand_3_out;

  nand nand_1 (nand_1_out, 1'b1, 1'b1);
  nand nand_2 (nand_2_out, 1'b1, 1'b1);
  nand nand_3 (nand_3_out, nand_1_out, nand_2_out);
  // Probe on nand_3_out
endmodule
