// Logisim project Shift Register.circ as structural Verilog: 1 circuit, main circuit main
module main (
);

  wire clock_1_out, clock_2_out, clock_3_out, nand_1_out, nand_2_out, nand_3_out, nand_4_out, nand_5_out,
       nand_6_out, nand_7_out, nand_8_out, nand_9_out, nand_10_out, nand_11_out, nand_12_out, nand_13_out,
       nand_14_out, nand_15_out, nand_16_out, nand_17_out, nand_18_out, nand_19_out, nand_20_out,
       nand_21_out, nand_22_out, nand_23_out, nand_24_out, nand_25_out, nand_26_out, nand_27_out;

  Clock clock_1 (.out(clock_1_out));
  Clock clock_2 (.out(clock_2_out));
  Clock clock_3 (.out(clock_3_out));
  nand nand_1 (nand_1_out, 1'b1, clock_1_out);
  nand nand_2 (nand_2_out, nand_1_out, clock_1_out);
  nand nand_3 (nand_3_out, nand_22_out, clock_2_out);
  nand nand_4 (nand_4_out, nand_3_out, clock_2_out);
  nand nand_5 (nand_5_out, nand_24_out, clock_3_out);
  nand nand_6 (nand_6_out, nand_5_out, clock_3_out);
  nand nand_7 (nand_7_out, nand_1_out, nand_8_out);
  nand nand_8 (nand_8_out, nand_7_out, nand_2_out);
  nand nand_9 (nand_9_out, clock_1_out, clock_1_out);
  nand nand_10 (nand_10_out, nand_3_out, nand_11_out);
  nand nand_11 (nand_11_out, nand_10_out, nand_4_out);
  nand nand_12 (nand_12_out, clock_2_out, clock_2_out);
  nand nand_13 (nand_13_out, nand_5_out, nand_14_out);
  nand nand_14 (nand_14_out, nand_13_out, nand_6_out);
  nand nand_15 (nand_15_out, clock_3_out, clock_3_out);
  nand nand_16 (nand_16_out, nand_7_out, nand_9_out);
  nand nand_17 (nand_17_out, nand_16_out, nand_9_out);
  nand nand_18 (nand_18_out, nand_10_out, nand_12_out);
  nand nand_19 (nand_19_out, nand_18_out, nand_12_out);
  nand nand_20 (nand_20_out, nand_13_out, nand_15_out);
  nand nand_21 (nand_21_out, nand_20_out, nand_15_out);
  nand nand_22 (nand_22_out, nand_16_out, nand_23_out);
  nand nand_23 (nand_23_out, nand_22_out, nand_17_out);
  nand nand_24 (nand_24_out, nand_18_out, nand_25_out);
  nand nand_25 (nand_25_out, nand_24_out, nand_19_out);
  nand nand_26 (nand_26_out, nand_20_out, nand_27_out);
  nand nand_27 (nand_27_out, nand_26_out, nand_21_out);
  // Probe on nand_22_out
  // Probe on nand_23_out
  // Probe on nand_24_out
  // Probe on nand_25_out
  // Probe on nand_26_out
  // Probe on nand_27_out

  // Notes on the sheet:
  //   D - DATA
  //   E - ENABLE
  //   D - DATA
  //   E - ENABLE
  //   D - DATA
  //   E - ENABLE
endmodule
